# Fritzing sketch Esquema Sensor y LED (saved by Fritzing 0.9.3b)
breadboards: 1

parts:
  Componente1 = Arduino Ethernet Shield (Rev3)
  T1 = LM35 Temperature Sensor [package="TO92 [THT]"]
  LED1 = smd LED [color="Red (633nm)" package="1206 [SMD]"]
  R1 = Resistor [tolerance=±5% resistance=220 package="2010 [SMD]"]

nets:
  GND: Componente1.GND, T1.GND, LED1.cathode
  N1: Componente1.D2, T1.Vout
  N2: Componente1.PWM_D3, R1.Pin_1
  N3: Componente1.5V, T1.+Vs
  N4: LED1.anode, R1.Pin_0
