# Fritzing sketch ProbandoLed (saved by Fritzing 0.9.3b)
breadboards: 1

parts:
  Componente1 = Arduino Uno (Rev3) [part_number=1]
  LED1 = smd LED [color="Red (633nm)" package="0805 [SMD]"]
  R1 = Resistor [tolerance=±5% resistance=220 package="0402 [SMD]"]

nets:
  N1: Componente1.GND, LED1.anode
  N2: Componente1.D3_PWM, R1.Pin_0
  N3: LED1.cathode, R1.Pin_1

// code stored in the sketch: Pruebaτ.ino
void setup() {
// initialize digital pin LED_BUILTIN as an output.
pinMode(PUERTO_LED, OUTPUT);
}
// the loop function runs over and over again forever
void loop() {
digitalWrite(PUERTO_LED, HIGH); // turn the LED on (HIGH is the voltage level)
delay(1000); // wait for a second
digitalWrite(PUERTO_LED, LOW); // turn the LED off by making the voltage LOW
delay(1000); // wait for a second
}

// code stored in the sketch: Prueba?.ino
void setup() {
// initialize digital pin LED_BUILTIN as an output.
pinMode(PUERTO_LED, OUTPUT);
}
// the loop function runs over and over again forever
void loop() {
digitalWrite(PUERTO_LED, HIGH); // turn the LED on (HIGH is the voltage level)
delay(1000); // wait for a second
digitalWrite(PUERTO_LED, LOW); // turn the LED off by making the voltage LOW
delay(1000); // wait for a second
}
